// Logisim project control.circ as structural Verilog: 1 circuit, main circuit control unit
module control_unit (
  input  start,
  input  \continue ,
  input  P0isOne,
  input  P0isZero,
  input  clock,
  output S_MS32B,
  output S_LS32B,
  output L_n,
  output S_n,
  output S_add,
  output L_LS32B,
  output L_MS32B,
  output L_multiplicand,
  output L_multiplier,
  output S_shift
);

  wire and_2_out, and_3_out, and_4_out, and_6_out, and_7_out, and_8_out, and_9_out, and_10_out, and_14_out,
       and_16_out, and_17_out, and_18_out, and_19_out, and_20_out, and_21_out, and_22_out, and_23_out,
       and_24_out, not_1_out, not_2_out, not_3_out, not_4_out, not_5_out, not_6_out, not_7_out, or_1_out,
       or_2_out, xnor_1_out, xor_1_out, xor_2_out, xor_3_out;
  wire [3:0] or_3_out, state_q;

  not not_1 (not_1_out, \continue );
  not not_2 (not_2_out, P0isOne);
  not not_3 (not_3_out, P0isZero);
  not not_4 (not_4_out, state_q[3]);
  not not_5 (not_5_out, state_q[2]);
  not not_6 (not_6_out, state_q[1]);
  not not_7 (not_7_out, state_q[0]);
  Register #(.width(4)) state (.D(or_3_out), .en(1'b1), .Q(state_q), .clk(clock));  // open: clr
  and and_1 (S_LS32B, not_4_out, state_q[2], state_q[1], state_q[0]);
  xor xor_1 (xor_1_out, state_q[3], state_q[1]);
  and and_2 (and_2_out, not_7_out, not_6_out, state_q[2]);
  and and_3 (and_3_out, state_q[0], state_q[1], not_5_out);
  xor xor_2 (xor_2_out, state_q[0], state_q[1]);
  xor xor_3 (xor_3_out, state_q[3], state_q[0]);
  and and_4 (and_4_out, state_q[2], not_4_out);
  xnor xnor_1 (xnor_1_out, state_q[2], state_q[0]);
  and and_5 (L_multiplicand, state_q[0], not_6_out, not_5_out, not_4_out);
  and and_6 (and_6_out, state_q[2], not_4_out, xor_2_out);
  and and_7 (and_7_out, not_7_out, not_6_out, not_4_out);
  and and_8 (and_8_out, P0isOne, not_3_out, state_q[2]);
  and and_9 (and_9_out, start, not_5_out);
  and and_10 (and_10_out, not_7_out, not_6_out, not_5_out, state_q[3]);
  and and_11 (L_n, xor_3_out, not_6_out, not_5_out);
  and and_12 (S_n, state_q[0], not_4_out, not_6_out, not_5_out);
  and and_13 (L_LS32B, xnor_1_out, state_q[1], not_4_out);
  or or_1 (or_1_out, and_2_out, and_3_out);
  and and_14 (and_14_out, not_4_out, xor_2_out);
  and and_15 (S_add, not_6_out, and_4_out);
  and and_16 (and_16_out, or_1_out, not_2_out, P0isZero, not_4_out);
  and and_17 (and_17_out, P0isOne, not_3_out, not_4_out, or_1_out);
  or or_2 (or_2_out, and_8_out, and_9_out);
  and and_18 (and_18_out, xor_1_out, not_7_out, not_5_out);
  and and_19 (and_19_out, xor_2_out, state_q[2], not_4_out);
  and and_20 (and_20_out, not_1_out, and_10_out);
  and and_21 (and_21_out, \continue , and_10_out);
  and and_22 (and_22_out, and_7_out, or_2_out);
  and and_23 (and_23_out, state_q[0], state_q[1], state_q[2], not_4_out);
  and and_24 (and_24_out, not_2_out, P0isZero, not_4_out, or_1_out);
  and and_25 (S_shift, and_14_out, state_q[2]);
  or or_3 (or_3_out[0], and_22_out, and_18_out, and_19_out);
  or or_4 (or_3_out[3], and_23_out, and_20_out);
  or or_5 (or_3_out[1], and_21_out, and_24_out, and_14_out);
  or or_6 (or_3_out[2], and_6_out, and_16_out, and_17_out);

  assign L_MS32B = L_LS32B;
  assign L_multiplier = L_multiplicand;
  assign S_MS32B = S_LS32B;

  // Notes on the sheet:
  //   P3'
  //   P3
  //   P2'
  //   P1
  //   P2
  //   P1'
  //   P0
  //   P0'
  //   P3 xor P1
  //   P3'.P2
  //   P3.P2'.P1'.P0'
  //   P2.P1'.P0'
  //   P2'.P1.P0
  //   P1 xor P0
  //   P3'.P2.P1.P0
  //   P2'.P1'.(P3 xor P0)
  //   P3'.P2'.P1'.P0
  //   P3'.P2.(P1 xor P0)
  //   P3'.P1'.P0'
  //   P2.P0isZero'.P0isOne
  //   P2'.S
  //   P3'.P2'.P1'.P0
  //   P3'.P1.(P2 xnor P0)
  //   P3'
  //   P2.P1'.P0' + P2'.P1.P0
  //   P3'. (P1 xor P0)
  //   P2'.P0'.(P3 xor P1)
  //   P3'.P2.(P1 xor P0)
  //   P3'.P2.P1.P0
  //   P3.P2'.P1'.P0'.C'
  //   P3.P2'.P1'.P0'.C
  //   P3'.P2.P1'
  //   P3'.P0isZero.P0isOne'.(P2'.P1.P0 + P2.P1'.P0')
  //   P3'.P0isZero'.P0isOne.(P2'.P1.P0 + P2.P1'.P0')
  //   N0
  //   P3'.P2.(P1 xor P0)
  //   N3
  //   N1
  //   N2
endmodule
