// Logisim project datapath.circ as structural Verilog: 8 circuits, main circuit main
module main (
  input  LMSB32,
  input  S_add,
  input  S_shift,
  input  Select_LS32B,
  input  LLSB32,
  input  [31:0] zero,
  input  Select_MS32B,
  input  Clock,
  input  [31:0] Input_A,
  input  Lmultiplicand,
  input  [31:0] Input_B,
  input  Lmultiplier,
  input  L_n,
  input  start_n,
  output P0isOne,
  output P0isZero,
  output [31:0] result_msb,
  output [31:0] result_lsb,
  output \continue ,
  output [5:0] counter_result
);

  wire not_1_out;
  wire [5:0] multiplexer_1_out, multiplexer_2_out, n6_bit_adder_1_result;
  wire [31:0] multiplexer_3_out, multiplexer_4_out, multiplexer_5_out, multiplicand_reg_q, multiplier_reg_q,
       n32_bit_adder_1_out_4, n64_bit_shifter_1_result_lsb, n64_bit_shifter_1_result_msb, register_1_q,
       register_2_q;

  Multiplexer #(.width(6), .enable("false")) multiplexer_1 (
    .in0(n6_bit_adder_1_result), .in1({6{1'b0}}), .out(multiplexer_1_out), .sel(start_n));
  Register #(.width(32)) multiplicand_reg (
    .D(Input_A), .en(Lmultiplicand), .Q(multiplicand_reg_q), .clk(Clock));  // open: clr
  Register #(.width(32)) multiplier_reg (
    .D(Input_B), .en(Lmultiplier), .Q(multiplier_reg_q), .clk(Clock));  // open: clr
  Register #(.width(6)) counter_reg (.D(multiplexer_1_out), .en(L_n), .Q(counter_result), .clk(Clock));  // open: clr
  Multiplexer #(.width(6), .enable("false")) multiplexer_2 (
    .in0(6'b000001), .in1({6{1'b0}}), .out(multiplexer_2_out), .sel(start_n));
  Multiplexer #(.width(32), .enable("false")) multiplexer_3 (
    .in0(zero), .in1(register_1_q), .out(multiplexer_3_out), .sel(Select_MS32B));
  Register #(.width(32)) MS32B_reg (.D(multiplexer_3_out), .en(LMSB32), .Q(result_msb), .clk(Clock));  // open: clr
  _6_bit_adder u_6_bit_adder_1 (
    .result(n6_bit_adder_1_result), .A_input(counter_result), .B_input(multiplexer_2_out), .clock(Clock));  // open: enable, cout
  _32_bit_adder u_32_bit_adder_1 (
    .in_1(result_msb), .in_2(multiplicand_reg_q), .out_4(n32_bit_adder_1_out_4), .enable(S_add));  // open: cout
  Multiplexer #(.width(32), .enable("false")) multiplexer_4 (
    .in0(result_msb), .in1(n32_bit_adder_1_out_4), .out(multiplexer_4_out), .sel(S_add));
  _64_bit_shifter u_64_bit_shifter_1 (
    .enable(S_shift), .MS32B(multiplexer_4_out), .LS32B(result_lsb),
    .result_msb(n64_bit_shifter_1_result_msb), .result_lsb(n64_bit_shifter_1_result_lsb));
  and and_1 (\continue , 1'b1, not_1_out);
  not not_1 (not_1_out, n6_bit_adder_1_result[5]);
  Register #(.width(32)) register_1 (.D(n64_bit_shifter_1_result_msb), .Q(register_1_q), .clk(Clock));  // open: en, clr
  Register #(.width(32)) register_2 (.D(n64_bit_shifter_1_result_lsb), .Q(register_2_q), .clk(Clock));  // open: en, clr
  Multiplexer #(.width(32), .enable("false")) multiplexer_5 (
    .in0(multiplier_reg_q), .in1(register_2_q), .out(multiplexer_5_out), .sel(Select_LS32B));
  Register #(.width(32)) LS32B_reg (.D(multiplexer_5_out), .en(LLSB32), .Q(result_lsb), .clk(Clock));  // open: clr
  comparator comparator_1 (.A___B_2(P0isOne), .A___B_3(P0isZero), .B(result_lsb[0]), .A(1'b0));  // open: A___B

  // Notes on the sheet:
  //   msb32b
endmodule

module comparator (
  input  B,
  input  A,
  output A___B,
  output A___B_2,
  output A___B_3
);

  wire A_prime_B_prime_out, AB_out, not_1_out, not_2_out;

  not not_1 (not_1_out, B);
  not not_2 (not_2_out, A);
  and A_prime_B_prime (A_prime_B_prime_out, not_1_out, not_2_out);
  and AB (AB_out, A, B);
  and u_A___B (A___B, A, not_1_out);
  and u_A___B_2 (A___B_2, not_2_out, B);
  or A_B (A___B_3, A_prime_B_prime_out, AB_out);
endmodule

module _1_bit_adder (
  input  Cin,
  input  A,
  input  B,
  output Si,
  output Cout
);

  wire and_1_out, and_2_out, xor_1_out;

  xor xor_1 (xor_1_out, A, B);
  xor xor_2 (Si, xor_1_out, Cin);
  and and_1 (and_1_out, Cin, xor_1_out);
  and and_2 (and_2_out, A, B);
  or or_1 (Cout, and_1_out, and_2_out);

  // Notes on the sheet:
  //   A XOR B
  //   A XOR B XOR C
  //   (A XOR B) AND C 
  //   A AND B
  //   ((A XOR B) AND C) OR (A AND B)
endmodule

module _32_bit_adder (
  input  [31:0] in_1,
  input  [31:0] in_2,
  input  enable,
  output [31:0] out_4,
  output cout
);

  wire clock_1_out, comparator_1_a___b_3, n1_bit_adder_1_cout, n1_bit_adder_2_cout, n1_bit_adder_3_cout,
       n1_bit_adder_4_cout, n1_bit_adder_5_cout, n1_bit_adder_6_cout, n1_bit_adder_7_cout,
       n1_bit_adder_8_cout, n1_bit_adder_9_cout, n1_bit_adder_10_cout, n1_bit_adder_11_cout,
       n1_bit_adder_12_cout, n1_bit_adder_13_cout, n1_bit_adder_14_cout, n1_bit_adder_15_cout,
       n1_bit_adder_16_cout, n1_bit_adder_17_cout, n1_bit_adder_18_cout, n1_bit_adder_19_cout,
       n1_bit_adder_20_cout, n1_bit_adder_21_cout, n1_bit_adder_22_cout, n1_bit_adder_23_cout,
       n1_bit_adder_24_cout, n1_bit_adder_25_cout, n1_bit_adder_26_cout, n1_bit_adder_27_cout,
       n1_bit_adder_28_cout, n1_bit_adder_29_cout, n1_bit_adder_30_cout, n1_bit_adder_31_cout;
  wire [31:0] register_1_q, register_2_q;

  comparator comparator_1 (.A___B_3(comparator_1_a___b_3), .B(enable), .A(1'b1));  // open: A___B, A___B_2
  Register #(.width(32)) register_1 (
    .D(in_1), .en(comparator_1_a___b_3), .Q(register_1_q), .clk(clock_1_out));  // open: clr
  Register #(.width(32)) register_2 (
    .D(in_2), .en(comparator_1_a___b_3), .Q(register_2_q), .clk(clock_1_out));  // open: clr
  Clock clock_1 (.out(clock_1_out));
  _1_bit_adder u_1_bit_adder_1 (
    .A(register_1_q[0]), .B(register_2_q[0]), .Si(out_4[0]), .Cin(1'b0), .Cout(n1_bit_adder_1_cout));
  _1_bit_adder u_1_bit_adder_2 (
    .A(register_1_q[1]), .B(register_2_q[1]), .Si(out_4[1]), .Cin(n1_bit_adder_1_cout),
    .Cout(n1_bit_adder_2_cout));
  _1_bit_adder u_1_bit_adder_3 (
    .A(register_1_q[2]), .B(register_2_q[2]), .Si(out_4[2]), .Cin(n1_bit_adder_2_cout),
    .Cout(n1_bit_adder_3_cout));
  _1_bit_adder u_1_bit_adder_4 (
    .A(register_1_q[3]), .B(register_2_q[3]), .Si(out_4[3]), .Cin(n1_bit_adder_3_cout),
    .Cout(n1_bit_adder_4_cout));
  _1_bit_adder u_1_bit_adder_5 (
    .A(register_1_q[4]), .B(register_2_q[4]), .Si(out_4[4]), .Cin(n1_bit_adder_4_cout),
    .Cout(n1_bit_adder_5_cout));
  _1_bit_adder u_1_bit_adder_6 (
    .A(register_1_q[5]), .B(register_2_q[5]), .Si(out_4[5]), .Cin(n1_bit_adder_5_cout),
    .Cout(n1_bit_adder_6_cout));
  _1_bit_adder u_1_bit_adder_7 (
    .A(register_1_q[6]), .B(register_2_q[6]), .Si(out_4[6]), .Cin(n1_bit_adder_6_cout),
    .Cout(n1_bit_adder_7_cout));
  _1_bit_adder u_1_bit_adder_8 (
    .A(register_1_q[7]), .B(register_2_q[7]), .Si(out_4[7]), .Cin(n1_bit_adder_7_cout),
    .Cout(n1_bit_adder_8_cout));
  _1_bit_adder u_1_bit_adder_9 (
    .A(register_1_q[8]), .B(register_2_q[8]), .Si(out_4[8]), .Cin(n1_bit_adder_8_cout),
    .Cout(n1_bit_adder_9_cout));
  _1_bit_adder u_1_bit_adder_10 (
    .A(register_1_q[9]), .B(register_2_q[9]), .Si(out_4[9]), .Cin(n1_bit_adder_9_cout),
    .Cout(n1_bit_adder_10_cout));
  _1_bit_adder u_1_bit_adder_11 (
    .A(register_1_q[10]), .B(register_2_q[10]), .Si(out_4[10]), .Cin(n1_bit_adder_10_cout),
    .Cout(n1_bit_adder_11_cout));
  _1_bit_adder u_1_bit_adder_12 (
    .A(register_1_q[11]), .B(register_2_q[11]), .Si(out_4[11]), .Cin(n1_bit_adder_11_cout),
    .Cout(n1_bit_adder_12_cout));
  _1_bit_adder u_1_bit_adder_13 (
    .A(register_1_q[12]), .B(register_2_q[12]), .Si(out_4[12]), .Cin(n1_bit_adder_12_cout),
    .Cout(n1_bit_adder_13_cout));
  _1_bit_adder u_1_bit_adder_14 (
    .A(register_1_q[13]), .B(register_2_q[13]), .Si(out_4[13]), .Cin(n1_bit_adder_13_cout),
    .Cout(n1_bit_adder_14_cout));
  _1_bit_adder u_1_bit_adder_15 (
    .A(register_1_q[14]), .B(register_2_q[14]), .Si(out_4[14]), .Cin(n1_bit_adder_14_cout),
    .Cout(n1_bit_adder_15_cout));
  _1_bit_adder u_1_bit_adder_16 (
    .A(register_1_q[15]), .B(register_2_q[15]), .Si(out_4[15]), .Cin(n1_bit_adder_15_cout),
    .Cout(n1_bit_adder_16_cout));
  _1_bit_adder u_1_bit_adder_17 (
    .A(register_1_q[16]), .B(register_2_q[16]), .Si(out_4[16]), .Cin(n1_bit_adder_16_cout),
    .Cout(n1_bit_adder_17_cout));
  _1_bit_adder u_1_bit_adder_18 (
    .A(register_1_q[17]), .B(register_2_q[17]), .Si(out_4[17]), .Cin(n1_bit_adder_17_cout),
    .Cout(n1_bit_adder_18_cout));
  _1_bit_adder u_1_bit_adder_19 (
    .A(register_1_q[18]), .B(register_2_q[18]), .Si(out_4[18]), .Cin(n1_bit_adder_18_cout),
    .Cout(n1_bit_adder_19_cout));
  _1_bit_adder u_1_bit_adder_20 (
    .A(register_1_q[19]), .B(register_2_q[19]), .Si(out_4[19]), .Cin(n1_bit_adder_19_cout),
    .Cout(n1_bit_adder_20_cout));
  _1_bit_adder u_1_bit_adder_21 (
    .A(register_1_q[20]), .B(register_2_q[20]), .Si(out_4[20]), .Cin(n1_bit_adder_20_cout),
    .Cout(n1_bit_adder_21_cout));
  _1_bit_adder u_1_bit_adder_22 (
    .A(register_1_q[21]), .B(register_2_q[21]), .Si(out_4[21]), .Cin(n1_bit_adder_21_cout),
    .Cout(n1_bit_adder_22_cout));
  _1_bit_adder u_1_bit_adder_23 (
    .A(register_1_q[22]), .B(register_2_q[22]), .Si(out_4[22]), .Cin(n1_bit_adder_22_cout),
    .Cout(n1_bit_adder_23_cout));
  _1_bit_adder u_1_bit_adder_24 (
    .A(register_1_q[23]), .B(register_2_q[23]), .Si(out_4[23]), .Cin(n1_bit_adder_23_cout),
    .Cout(n1_bit_adder_24_cout));
  _1_bit_adder u_1_bit_adder_25 (
    .A(register_1_q[24]), .B(register_2_q[24]), .Si(out_4[24]), .Cin(n1_bit_adder_24_cout),
    .Cout(n1_bit_adder_25_cout));
  _1_bit_adder u_1_bit_adder_26 (
    .A(register_1_q[25]), .B(register_2_q[25]), .Si(out_4[25]), .Cin(n1_bit_adder_25_cout),
    .Cout(n1_bit_adder_26_cout));
  _1_bit_adder u_1_bit_adder_27 (
    .A(register_1_q[26]), .B(register_2_q[26]), .Si(out_4[26]), .Cin(n1_bit_adder_26_cout),
    .Cout(n1_bit_adder_27_cout));
  _1_bit_adder u_1_bit_adder_28 (
    .A(register_1_q[27]), .B(register_2_q[27]), .Si(out_4[27]), .Cin(n1_bit_adder_27_cout),
    .Cout(n1_bit_adder_28_cout));
  _1_bit_adder u_1_bit_adder_29 (
    .A(register_1_q[28]), .B(register_2_q[28]), .Si(out_4[28]), .Cin(n1_bit_adder_28_cout),
    .Cout(n1_bit_adder_29_cout));
  _1_bit_adder u_1_bit_adder_30 (
    .A(register_1_q[29]), .B(register_2_q[29]), .Si(out_4[29]), .Cin(n1_bit_adder_29_cout),
    .Cout(n1_bit_adder_30_cout));
  _1_bit_adder u_1_bit_adder_31 (
    .A(register_1_q[30]), .B(register_2_q[30]), .Si(out_4[30]), .Cin(n1_bit_adder_30_cout),
    .Cout(n1_bit_adder_31_cout));
  _1_bit_adder u_1_bit_adder_32 (
    .A(register_1_q[31]), .B(register_2_q[31]), .Si(out_4[31]), .Cin(n1_bit_adder_31_cout), .Cout(cout));

  // Notes on the sheet:
  //   A
  //   B
  //   Result
endmodule

module _6_bit_adder (
  input  clock,
  input  enable,
  input  [5:0] A_input,
  input  [5:0] B_input,
  output [5:0] result,
  output cout
);

  wire comparator_1_a___b_3, n1_bit_adder_1_cout, n1_bit_adder_2_cout, n1_bit_adder_3_cout,
       n1_bit_adder_4_cout, n1_bit_adder_5_cout;
  wire [5:0] register_1_q, register_2_q;

  comparator comparator_1 (.A___B_3(comparator_1_a___b_3), .B(enable), .A(1'b1));  // open: A___B, A___B_2
  Register #(.width(6)) register_1 (
    .D(A_input), .en(comparator_1_a___b_3), .Q(register_1_q), .clk(clock));  // open: clr
  Register #(.width(6)) register_2 (
    .D(B_input), .en(comparator_1_a___b_3), .Q(register_2_q), .clk(clock));  // open: clr
  _1_bit_adder u_1_bit_adder_1 (
    .A(register_1_q[0]), .B(register_2_q[0]), .Si(result[0]), .Cin(1'b0), .Cout(n1_bit_adder_1_cout));
  _1_bit_adder u_1_bit_adder_2 (
    .A(register_1_q[1]), .B(register_2_q[1]), .Si(result[1]), .Cin(n1_bit_adder_1_cout),
    .Cout(n1_bit_adder_2_cout));
  _1_bit_adder u_1_bit_adder_3 (
    .A(register_1_q[2]), .B(register_2_q[2]), .Si(result[2]), .Cin(n1_bit_adder_2_cout),
    .Cout(n1_bit_adder_3_cout));
  _1_bit_adder u_1_bit_adder_4 (
    .A(register_1_q[3]), .B(register_2_q[3]), .Si(result[3]), .Cin(n1_bit_adder_3_cout),
    .Cout(n1_bit_adder_4_cout));
  _1_bit_adder u_1_bit_adder_5 (
    .A(register_1_q[4]), .B(register_2_q[4]), .Si(result[4]), .Cin(n1_bit_adder_4_cout),
    .Cout(n1_bit_adder_5_cout));
  _1_bit_adder u_1_bit_adder_6 (
    .A(register_1_q[5]), .B(register_2_q[5]), .Si(result[5]), .Cin(n1_bit_adder_5_cout), .Cout(cout));
endmodule

module _32_bit_shifter (
  input  [31:0] \input ,
  input  lsb,
  input  enable,
  output [31:0] result
);

  _2x1_mux u_2x1_mux_1 (.Result(result[31]), .S(enable), .I1(lsb), .I0(\input [31]));
  _2x1_mux u_2x1_mux_2 (.Result(result[29]), .S(enable), .I1(\input [30]), .I0(\input [29]));
  _2x1_mux u_2x1_mux_3 (.Result(result[30]), .S(enable), .I1(\input [31]), .I0(\input [30]));
  _2x1_mux u_2x1_mux_4 (.Result(result[27]), .S(enable), .I1(\input [28]), .I0(\input [27]));
  _2x1_mux u_2x1_mux_5 (.Result(result[28]), .S(enable), .I1(\input [29]), .I0(\input [28]));
  _2x1_mux u_2x1_mux_6 (.Result(result[25]), .S(enable), .I1(\input [26]), .I0(\input [25]));
  _2x1_mux u_2x1_mux_7 (.Result(result[26]), .S(enable), .I1(\input [27]), .I0(\input [26]));
  _2x1_mux u_2x1_mux_8 (.Result(result[24]), .S(enable), .I1(\input [25]), .I0(\input [24]));
  _2x1_mux u_2x1_mux_9 (.Result(result[23]), .S(enable), .I1(\input [24]), .I0(\input [23]));
  _2x1_mux u_2x1_mux_10 (.Result(result[22]), .S(enable), .I1(\input [23]), .I0(\input [22]));
  _2x1_mux u_2x1_mux_11 (.Result(result[21]), .S(enable), .I1(\input [22]), .I0(\input [21]));
  _2x1_mux u_2x1_mux_12 (.Result(result[20]), .S(enable), .I1(\input [21]), .I0(\input [20]));
  _2x1_mux u_2x1_mux_13 (.Result(result[19]), .S(enable), .I1(\input [20]), .I0(\input [19]));
  _2x1_mux u_2x1_mux_14 (.Result(result[18]), .S(enable), .I1(\input [19]), .I0(\input [18]));
  _2x1_mux u_2x1_mux_15 (.Result(result[17]), .S(enable), .I1(\input [18]), .I0(\input [17]));
  _2x1_mux u_2x1_mux_16 (.Result(result[15]), .S(enable), .I1(\input [16]), .I0(\input [15]));
  _2x1_mux u_2x1_mux_17 (.Result(result[16]), .S(enable), .I1(\input [17]), .I0(\input [16]));
  _2x1_mux u_2x1_mux_18 (.Result(result[13]), .S(enable), .I1(\input [14]), .I0(\input [13]));
  _2x1_mux u_2x1_mux_19 (.Result(result[14]), .S(enable), .I1(\input [15]), .I0(\input [14]));
  _2x1_mux u_2x1_mux_20 (.Result(result[11]), .S(enable), .I1(\input [12]), .I0(\input [11]));
  _2x1_mux u_2x1_mux_21 (.Result(result[12]), .S(enable), .I1(\input [13]), .I0(\input [12]));
  _2x1_mux u_2x1_mux_22 (.Result(result[9]), .S(enable), .I1(\input [10]), .I0(\input [9]));
  _2x1_mux u_2x1_mux_23 (.Result(result[10]), .S(enable), .I1(\input [11]), .I0(\input [10]));
  _2x1_mux u_2x1_mux_24 (.Result(result[8]), .S(enable), .I1(\input [9]), .I0(\input [8]));
  _2x1_mux u_2x1_mux_25 (.Result(result[7]), .S(enable), .I1(\input [8]), .I0(\input [7]));
  _2x1_mux u_2x1_mux_26 (.Result(result[6]), .S(enable), .I1(\input [7]), .I0(\input [6]));
  _2x1_mux u_2x1_mux_27 (.Result(result[5]), .S(enable), .I1(\input [6]), .I0(\input [5]));
  _2x1_mux u_2x1_mux_28 (.Result(result[3]), .S(enable), .I1(\input [4]), .I0(\input [3]));
  _2x1_mux u_2x1_mux_29 (.Result(result[4]), .S(enable), .I1(\input [5]), .I0(\input [4]));
  _2x1_mux u_2x1_mux_30 (.Result(result[2]), .S(enable), .I1(\input [3]), .I0(\input [2]));
  _2x1_mux u_2x1_mux_31 (.Result(result[1]), .S(enable), .I1(\input [2]), .I0(\input [1]));
  _2x1_mux u_2x1_mux_32 (.Result(result[0]), .S(enable), .I1(\input [1]), .I0(\input [0]));
endmodule

module _2x1_mux (
  input  S,
  input  I1,
  input  I0,
  output Result
);

  wire and_1_out, and_2_out, not_1_out;

  not not_1 (not_1_out, S);
  and and_1 (and_1_out, I1, S);
  and and_2 (and_2_out, I0, not_1_out);
  or or_1 (Result, and_1_out, and_2_out);
endmodule

module _64_bit_shifter (
  input  [31:0] MS32B,
  input  [31:0] LS32B,
  input  enable,
  output [31:0] result_msb,
  output [31:0] result_lsb
);

  _32_bit_shifter u_32_bit_shifter_1 (.\input (MS32B), .enable(enable), .result(result_msb), .lsb(1'b0));
  _32_bit_shifter u_32_bit_shifter_2 (.\input (LS32B), .enable(enable), .result(result_lsb), .lsb(MS32B[0]));
endmodule
