// Logisim project mult32.circ as structural Verilog: 1 circuit, main circuit main
module main (
  input  [31:0] input_A,
  input  [31:0] input_B,
  input  [31:0] in_3,
  output [31:0] out_4,
  output [31:0] out_5,
  output [5:0] n_counter
);

  wire button_1_out, clk_out, control_unit_1_l_ls32b, control_unit_1_l_ms32b, control_unit_1_l_multiplicand,
       control_unit_1_l_multiplier, control_unit_1_l_n, control_unit_1_s_add, control_unit_1_s_ls32b,
       control_unit_1_s_ms32b, control_unit_1_s_n, control_unit_1_s_shift, main_1_continue, main_1_p0isone,
       main_1_p0iszero;

  Button button_1 (.out(button_1_out));
  Clock clk (.out(clk_out));
  control_unit control_unit_1 (
    .clock(clk_out), .start(button_1_out), .\continue (main_1_continue), .P0isOne(main_1_p0isone),
    .P0isZero(main_1_p0iszero), .S_MS32B(control_unit_1_s_ms32b), .S_LS32B(control_unit_1_s_ls32b),
    .L_n(control_unit_1_l_n), .S_n(control_unit_1_s_n), .S_add(control_unit_1_s_add),
    .L_LS32B(control_unit_1_l_ls32b), .L_MS32B(control_unit_1_l_ms32b),
    .L_multiplicand(control_unit_1_l_multiplicand), .L_multiplier(control_unit_1_l_multiplier),
    .S_shift(control_unit_1_s_shift));
  datapath_main main_1 (
    .zero(in_3), .Select_MS32B(control_unit_1_s_ms32b), .Clock(clk_out), .Input_A(input_A),
    .Lmultiplicand(control_unit_1_l_multiplicand), .Input_B(input_B),
    .Lmultiplier(control_unit_1_l_multiplier), .L_n(control_unit_1_l_n), .start_n(control_unit_1_s_n),
    .P0isOne(main_1_p0isone), .P0isZero(main_1_p0iszero), .result_msb(out_4), .result_lsb(out_5),
    .\continue (main_1_continue), .counter_result(n_counter), .LMSB32(control_unit_1_l_ms32b),
    .S_add(control_unit_1_s_add), .S_shift(control_unit_1_s_shift), .Select_LS32B(control_unit_1_s_ls32b),
    .LLSB32(control_unit_1_l_ls32b));

  // Notes on the sheet:
  //   start button
  //   product MS32B
  //   product LS32B
endmodule
